# Fritzing sketch haptics (saved by Fritzing 0.9.3b)
breadboards: 1

parts:
  Procedure_Arm_LED = LED - 5mm [color="Green (570nm)" package="5 mm [THT]"]
  Error_LED = LED - 5mm [color="Red (633nm)" package="5 mm [THT]"]
  Timing_LED = LED - 5mm [color="Yellow (595nm)" package="5 mm [THT]"]
  Play_arm_transistor = Basic FET N-Channel [package="TO220 [THT]"]
  R1 = Resistor [tolerance=±5% resistance=270 package="2010 [SMD]"]
  PC_C2_1 = Vibration Motor- ROB-08449 [package=vibe-motor-10mm]
  Procedure_arm_transistor = Basic FET N-Channel [package="TO220 [THT]"]
  R2 = Resistor [tolerance=±5% resistance=270 package="2010 [SMD]"]
  R3 = Resistor [tolerance=±5% resistance=270 package="2010 [SMD]"]
  R4 = Resistor [tolerance=±5% resistance=10k package="2010 [SMD]"]
  R5 = Resistor [tolerance=±5% resistance=10k package="2010 [SMD]"]
  Procedure_arm_diode = Diode [package=diode-hv]
  PC_C2_5 = Vibration Motor- ROB-08449 [package=vibe-motor-10mm]
  PC_C2_4 = Vibration Motor- ROB-08449 [package=vibe-motor-10mm]
  PC_C2_3 = Vibration Motor- ROB-08449 [package=vibe-motor-10mm]
  PC_C2_2 = Vibration Motor- ROB-08449 [package=vibe-motor-10mm]
  PL_C2_2 = Vibration Motor- ROB-08449 [package=vibe-motor-10mm]
  PL_C2_3 = Vibration Motor- ROB-08449 [package=vibe-motor-10mm]
  PL_C2_4 = Vibration Motor- ROB-08449 [package=vibe-motor-10mm]
  PL_C2_5 = Vibration Motor- ROB-08449 [package=vibe-motor-10mm]
  Arduino_Uno = Arduino Uno (Rev3)
  PL_C2_1 = Vibration Motor- ROB-08449 [package=vibe-motor-10mm]
  R6 = Resistor [tolerance=±5% resistance=10 package="2010 [SMD]"]
  R7 = Resistor [tolerance=±5% resistance=10 package="2010 [SMD]"]
  R8 = Resistor [tolerance=±5% resistance=10 package="2010 [SMD]"]
  R9 = Resistor [tolerance=±5% resistance=10 package="2010 [SMD]"]
  R10 = Resistor [tolerance=±5% resistance=10 package="2010 [SMD]"]
  R11 = Resistor [tolerance=±5% resistance=10 package="2010 [SMD]"]
  R12 = Resistor [tolerance=±5% resistance=10 package="2010 [SMD]"]
  R13 = Resistor [tolerance=±5% resistance=10 package="2010 [SMD]"]
  R14 = Resistor [tolerance=±5% resistance=10 package="2010 [SMD]"]
  R15 = Resistor [tolerance=±5% resistance=10 package="2010 [SMD]"]
  play_arm_diode = Diode [package=diode-hv]
  5v_powerbank = Lilypad Power Supply

nets:
  N1: Procedure_Arm_LED.cathode, R3.Pin_0
  N2: Procedure_Arm_LED.anode, Procedure_arm_transistor.gate, R4.Pin_0, Arduino_Uno.D3_PWM
  N3: Error_LED.cathode, R1.Pin_0
  N4: Error_LED.anode, Arduino_Uno.D7
  N5: Timing_LED.cathode, R2.Pin_0
  N6: Timing_LED.anode, Arduino_Uno.D8
  N7: Play_arm_transistor.gate, R5.Pin_0, Arduino_Uno.D5_PWM
  N8: Play_arm_transistor.drain, Procedure_arm_diode.C, PL_C2_2.-, PL_C2_3.-, PL_C2_4.-, PL_C2_5.-, PL_C2_1.-
  GND: Play_arm_transistor.source, R1.Pin_1, Procedure_arm_transistor.source, R2.Pin_1, R3.Pin_1, R4.Pin_1, R5.Pin_1, Arduino_Uno.GND, 5v_powerbank.GND
  N9: PC_C2_1.+, R10.Pin_0
  N10: PC_C2_1.-, Procedure_arm_transistor.drain, PC_C2_5.-, PC_C2_4.-, PC_C2_3.-, PC_C2_2.-, play_arm_diode.C
  N11: Procedure_arm_diode.A, R6.Pin_1, R7.Pin_1, R8.Pin_1, R9.Pin_1, R10.Pin_1, R11.Pin_1, R12.Pin_1, R13.Pin_1, R14.Pin_1, R15.Pin_1, play_arm_diode.A, 5v_powerbank.+
  N12: PC_C2_5.+, R9.Pin_0
  N13: PC_C2_4.+, R6.Pin_0
  N14: PC_C2_3.+, R7.Pin_0
  N15: PC_C2_2.+, R8.Pin_0
  N16: PL_C2_2.+, R14.Pin_0
  N17: PL_C2_3.+, R13.Pin_0
  N18: PL_C2_4.+, R12.Pin_0
  N19: PL_C2_5.+, R11.Pin_0
  N20: PL_C2_1.+, R15.Pin_0
